# Fritzing sketch dum.bot (saved by Fritzing 0.9.1b)

parts:
  Raspberry_Pi1 = Raspberry Pi B rev2
  J1 = Basic Servo
  J2 = Basic Servo
  M2 = DC Motor
  TRINKET1 = Trinket 3V
  VCC1 = 4 x AAA Battery Mount
  S1 = H-Bridge with L298N
  M1 = DC Motor

nets:
  N1: Raspberry_Pi1.GPIO_2, TRINKET1.no_name_yet#9
  N2: Raspberry_Pi1.GPIO_3, TRINKET1.no_name_yet#7
  GND: Raspberry_Pi1.GND, J1.gnd, J2.gnd, TRINKET1.no_name_yet#2, VCC1.-, S1.GND
  N3: Raspberry_Pi1.GPIO_10, S1.IN2
  N4: Raspberry_Pi1.GPIO_9, S1.IN1
  N5: Raspberry_Pi1.GPIO_11, S1.IN3
  N6: Raspberry_Pi1.GPIO_8, S1.IN4
  VCC: J1.vcc, J2.vcc, VCC1.+, S1.5V
  N7: J1.pulse, TRINKET1.no_name_yet#3
  N8: J2.pulse, TRINKET1.no_name_yet#8
  N9: M2.pin_1, S1.M2-01
  N10: M2.pin_2, S1.M2-02
  N11: S1.M1-01, M1.pin_1
  N12: S1.M1-02, M1.pin_2

custom parts:
  Trinket 3V: Adafruit Trinket 3V
  H-Bridge with L298N: h-bridge
